// Logisim project CPU_pipeline_p1.circ as structural Verilog
module main (
  input  [4:0] in_1,
  input  in_2
);

  wire alu_1_zero, and_1_out, clock_1_out, d_ff_1_q, exmem_1_aluzero_out, harzard_1_stall,
       multiplexer_10_out, not_1_out, or_2_out;
  wire [1:0] control_unit_1_aluop, control_unit_1_alusrc, control_unit_1_regsrc, forward_1_forwarda,
       forward_1_forwardb, or_1_out;
  wire [2:0] exmem_1_wb_out, idex_1_wb_out, memwb_1_wb_out, multiplexer_5_out;
  wire [2:2] control_unit_1_regwrite;
  wire [3:0] alu_control_1_control, idex_1_alucontrol_out, idex_1_exout, ifid_1_instruction_out_6,
       multiplexer_4_out;
  wire [4:0] exmem_1_memory_out, exmem_1_wb_address_out, idex_1_rs1_address_out, idex_1_rs2_address_out,
       idex_1_wb_address_out, ifid_1_instruction_out, ifid_1_instruction_out_2, ifid_1_instruction_out_5,
       memwb_1_wb_address_out;
  wire [5:0] control_unit_1_memread, idex_1_memory_out, multiplexer_3_out;
  wire [6:0] ifid_1_instruction_out_4;
  wire [7:0] counter_1_q;
  wire [31:0] alu_1_result, exmem_1_aluresult_out, exmem_1_pc_out, exmem_1_pc_plus4_out, exmem_1_read2_out,
       idex_1_immgen_out, idex_1_pc_out, idex_1_pc_plus4_out, idex_1_read1_out, idex_1_read2_out,
       ifid_1_pc_out, ifid_1_pc_plus4_out, immgen_1_imm, memwb_1_aluresult_out, memwb_1_mem_read_out,
       memwb_1_pc_plus4_out, memwb_1_pc_plusaddress_out, multiplexer_1_out, multiplexer_2_out,
       multiplexer_6_out, multiplexer_7_out, multiplexer_8_out, multiplexer_9_out, multiplexer_11_out,
       pc2_1_pc_out, ram_1_dout, register_file_1_rega_data, register_file_1_regb_data,
       register_file_1_regmanual_data, rom_1_data, somador_1_z, somador_2_z;
  wire [31:25] ifid_1_instruction_out_3;

  Clock clock_1 (.out(clock_1_out));
  Multiplexer #(.width(32)) multiplexer_1 (
    .in0(multiplexer_2_out), .in1(somador_1_z), .out(multiplexer_1_out), .sel(d_ff_1_q));
  D_Flip_Flop d_ff_1 (.D(1'b0), .clk(clock_1_out), .Q(d_ff_1_q));  // open: Qn, preset, reset
  Counter counter_1 (.Q(counter_1_q), .clk(clock_1_out), .clr(in_2));  // open: load, D, count, carry, up
  PC2 pc2_1 (
    .clk(counter_1_q[0]), .reset(in_2), .pc_in(multiplexer_1_out), .writeEnable(harzard_1_stall),
    .pc_out(pc2_1_pc_out));
  ROM #(.addrWidth(24), .dataWidth(32)) rom_1 (.addr(pc2_1_pc_out[23:0]), .data(rom_1_data));
  somador somador_1 (.A(pc2_1_pc_out), .B(32'h1), .Z(somador_1_z));
  IFID ifid_1 (
    .clk(counter_1_q[0]), .PC_in(pc2_1_pc_out), .PC_plus4_in(somador_1_z), .writeEnable(harzard_1_stall),
    .instruction_In(rom_1_data), .PC_out(ifid_1_pc_out), .PC_plus4_out(ifid_1_pc_plus4_out),
    .instruction_Out({ifid_1_instruction_out_3[31], ifid_1_instruction_out_6[3], ifid_1_instruction_out_3[29:25], ifid_1_instruction_out, ifid_1_instruction_out_2, ifid_1_instruction_out_6[2:0], ifid_1_instruction_out_5, ifid_1_instruction_out_4}));
  // Probe on {ifid_1_instruction_out_3[31], ifid_1_instruction_out_6[3], ifid_1_instruction_out_3[29:25], ifid_1_instruction_out, ifid_1_instruction_out_2, ifid_1_instruction_out_6[2:0], ifid_1_instruction_out_5, ifid_1_instruction_out_4}
  Harzard harzard_1 (
    .clk(clock_1_out), .MemReadSignal_EX(idex_1_memory_out[0]), .RegRD_EX(idex_1_wb_address_out),
    .RegRs1(ifid_1_instruction_out_2), .RegRs2(ifid_1_instruction_out), .stall(harzard_1_stall));
  // Probe on register_file_1_regmanual_data
  register_file register_file_1 (
    .\input (multiplexer_11_out), .regManual_selector(in_1), .writeEnable(memwb_1_wb_out[2]),
    .regA_selector(ifid_1_instruction_out_2), .regB_selector(ifid_1_instruction_out),
    .writeReg_selector(memwb_1_wb_address_out), .clk(clock_1_out), .regA_data(register_file_1_rega_data),
    .regB_data(register_file_1_regb_data), .RegManual_data(register_file_1_regmanual_data));
  ImmGen immgen_1 (
    .instruction({ifid_1_instruction_out_3[31], ifid_1_instruction_out_6[3], ifid_1_instruction_out_3[29:25], ifid_1_instruction_out, ifid_1_instruction_out_2, ifid_1_instruction_out_6[2:0], ifid_1_instruction_out_5, ifid_1_instruction_out_4}),
    .imm(immgen_1_imm));
  Control_Unit control_unit_1 (
    .opcode(ifid_1_instruction_out_4), .AluSrc(control_unit_1_alusrc[0]),
    .reg_zero(control_unit_1_alusrc[1]), .RegWrite(control_unit_1_regwrite[2]),
    .MemRead(control_unit_1_memread[0]), .MemWrite(control_unit_1_memread[1]),
    .Branch(control_unit_1_memread[2]), .BranchNotEq(control_unit_1_memread[3]),
    .BranchIncond(control_unit_1_memread[4]), .regToPC(control_unit_1_memread[5]),
    .AluOp(control_unit_1_aluop), .regSrc(control_unit_1_regsrc));
  Multiplexer #(.select(2), .width(32)) multiplexer_2 (
    .in0(somador_1_z), .in1(exmem_1_pc_out), .in2(exmem_1_aluresult_out), .in3(exmem_1_aluresult_out),
    .out(multiplexer_2_out), .sel(or_1_out));
  Multiplexer #(.width(6)) multiplexer_3 (
    .in0(control_unit_1_memread), .in1({6{1'b0}}), .out(multiplexer_3_out), .sel(harzard_1_stall));
  Multiplexer #(.width(4)) multiplexer_4 (
    .in0({control_unit_1_aluop, control_unit_1_alusrc}), .in1(4'b0000), .out(multiplexer_4_out),
    .sel(harzard_1_stall));
  Multiplexer #(.width(3)) multiplexer_5 (
    .in0({control_unit_1_regwrite[2], control_unit_1_regsrc}), .in1(3'b000), .out(multiplexer_5_out),
    .sel(harzard_1_stall));
  IDEX idex_1 (
    .clk(counter_1_q[0]), .PC_in(ifid_1_pc_out), .read1_in(register_file_1_rega_data),
    .read2_in(register_file_1_regb_data), .immGen_in(immgen_1_imm), .aluControl_in(ifid_1_instruction_out_6),
    .WB_address_in(ifid_1_instruction_out_5), .WB_in(multiplexer_5_out), .Memory_in(multiplexer_3_out),
    .EX_control_in(multiplexer_4_out), .PC_plus4_in(ifid_1_pc_plus4_out),
    .rs1_address_in(ifid_1_instruction_out_2), .rs2_address_in(ifid_1_instruction_out),
    .PC_out(idex_1_pc_out), .read1_out(idex_1_read1_out), .read2_out(idex_1_read2_out),
    .immGen_out(idex_1_immgen_out), .aluControl_out(idex_1_alucontrol_out),
    .WB_address_out(idex_1_wb_address_out), .WB_out(idex_1_wb_out), .Memory_out(idex_1_memory_out),
    .EXout(idex_1_exout), .PC_plus4_out(idex_1_pc_plus4_out), .rs1_address_out(idex_1_rs1_address_out),
    .rs2_address_out(idex_1_rs2_address_out));
  Multiplexer #(.width(32)) multiplexer_6 (
    .in0(idex_1_read1_out), .in1({32{1'b0}}), .out(multiplexer_6_out), .sel(idex_1_exout[1]));
  Multiplexer #(.width(32)) multiplexer_7 (
    .in0(idex_1_read2_out), .in1(idex_1_immgen_out), .out(multiplexer_7_out), .sel(idex_1_exout[0]));
  Multiplexer #(.select(2), .width(32)) multiplexer_8 (
    .in0(multiplexer_7_out), .in1(multiplexer_11_out), .in2(exmem_1_aluresult_out), .out(multiplexer_8_out),
    .sel(forward_1_forwardb));  // open: in3
  Multiplexer #(.select(2), .width(32)) multiplexer_9 (
    .in0(multiplexer_6_out), .in1(multiplexer_11_out), .in2(exmem_1_aluresult_out), .out(multiplexer_9_out),
    .sel(forward_1_forwarda));  // open: in3
  somador somador_2 (.A(idex_1_pc_out), .B(idex_1_immgen_out), .Z(somador_2_z));
  ALU alu_1 (
    .A(multiplexer_9_out), .B(multiplexer_8_out), .control(alu_control_1_control), .result(alu_1_result),
    .zero(alu_1_zero));
  ALU_Control alu_control_1 (.Funct(idex_1_alucontrol_out), .AluOp(idex_1_exout[3:2]), .Control(alu_control_1_control));
  Forward forward_1 (
    .clk(clock_1_out), .regWriteSignal_WB(memwb_1_wb_out[0]), .regWriteMEM(exmem_1_wb_out[0]),
    .RegRs1(idex_1_rs1_address_out), .RegRs2(idex_1_rs2_address_out), .RegRD_WB(memwb_1_wb_address_out),
    .RegRD_MEM(exmem_1_wb_address_out), .forwardA(forward_1_forwarda), .forwardB(forward_1_forwardb));
  EXMEM exmem_1 (
    .clk(counter_1_q[0]), .Sum_address_in(somador_2_z), .ALUzero_in(alu_1_zero), .ALUresult_in(alu_1_result),
    .read2_in(idex_1_read2_out), .WB_address_in(idex_1_wb_address_out), .WB_in(idex_1_wb_out),
    .Memory_in(idex_1_memory_out), .PC_plus4_in(idex_1_pc_plus4_out), .PC_out(exmem_1_pc_out),
    .ALUzero_out(exmem_1_aluzero_out), .ALUresult_out(exmem_1_aluresult_out), .read2_out(exmem_1_read2_out),
    .WB_address_out(exmem_1_wb_address_out), .WB_out(exmem_1_wb_out),
    .Memory_out({or_1_out[1], exmem_1_memory_out}), .PC_plus4_out(exmem_1_pc_plus4_out));
  or or_1 (or_1_out[0], exmem_1_memory_out[4], and_1_out);
  and and_1 (and_1_out, or_2_out, multiplexer_10_out);
  or or_2 (or_2_out, exmem_1_memory_out[2], exmem_1_memory_out[3]);
  Multiplexer multiplexer_10 (
    .in0(exmem_1_aluzero_out), .in1(not_1_out), .out(multiplexer_10_out), .sel(exmem_1_memory_out[3]));
  not not_1 (not_1_out, exmem_1_aluzero_out);
  RAM #(.addrWidth(24), .dataWidth(32)) ram_1 (
    .addr(exmem_1_aluresult_out[23:0]), .we(exmem_1_memory_out[1]), .oe(exmem_1_memory_out[0]),
    .clk(clock_1_out), .din(exmem_1_read2_out), .dout(ram_1_dout));
  MEMWB memwb_1 (
    .clk(counter_1_q[0]), .mem_read_in(ram_1_dout), .ALUresult_in(exmem_1_aluresult_out),
    .WB_address_in(exmem_1_wb_address_out), .WB_in(exmem_1_wb_out), .PC_plus4_in(exmem_1_pc_plus4_out),
    .PC_plusAddress_in(exmem_1_pc_out), .mem_read_out(memwb_1_mem_read_out),
    .ALUresult_out(memwb_1_aluresult_out), .WB_address_out(memwb_1_wb_address_out), .WB_out(memwb_1_wb_out),
    .PC_plus4_out(memwb_1_pc_plus4_out), .PC_plusAddress_out(memwb_1_pc_plusaddress_out));
  Multiplexer #(.select(2), .width(32)) multiplexer_11 (
    .in0(memwb_1_aluresult_out), .in1(memwb_1_mem_read_out), .in2(memwb_1_pc_plus4_out),
    .in3(memwb_1_pc_plusaddress_out), .out(multiplexer_11_out), .sel(memwb_1_wb_out[1:0]));

  // Notes on the sheet:
  //   contents of rom_1 (hex, n*v repeats v):
  //   9563                                                            -- Valor que é armazenado no
  //   endereço inicial da ROM
endmodule

// VHDL entity ALU, as the project stores it:
library IEEE;
use IEEE.STD_LOGIC_1164.ALL;
use ieee.numeric_std.ALL;
USE IEEE.std_logic_unsigned.ALL;

entity ALU is
    port(
    A, B      : in std_logic_vector(31 downto 0);  -- Entradas A e B de 32 bits
    control   : in std_logic_vector(3 downto 0);   -- Entrada de controle de 4 bits
    result    : out std_logic_vector(31 downto 0); -- Saída de resultado de 32 bits
    zero      : out std_logic);                    -- Saída para sinalizar se o resultado é zero
end ALU;

architecture TypeArchitecture of ALU is

signal zero_sig   : std_logic_vector(32 downto 0); -- Vetor para verificação de resultado zero
signal result_sig : std_logic_vector(31 downto 0); -- Vetor para armazenar o resultado da operação

begin
	
    result_sig <= (A + B) when control = "0010" else                -- Soma
    			   (A - B) when control = "0110" else                  -- Subtração
    			   (A XOR B) when control = "0101" else                -- XOR (ou exclusivo)
    			   (A OR B) when control = "0001" else                 -- OR (ou)
    			   (A AND B) when control = "0000" else                -- AND (e)
    			   (std_logic_vector(shift_left(unsigned(A), to_integer(unsigned(B))))) when control = "0011" else   -- Shift Left (deslocamento à esquerda)
    			   (std_logic_vector(shift_right(unsigned(A), to_integer(unsigned(B))))) when control = "0111";    -- Shift Right (deslocamento à direita)
        			
    result <= result_sig;                          -- Atribui o valor do resultado à saída result
    zero_sig(0) <= '0';                            -- Inicializa o primeiro bit de zero_sig como '0'
    G2: for I in 1 to 32 generate
            zero_sig(I) <= zero_sig(I - 1) or result_sig(I - 1);  -- Verificação de resultado zero bit a bit
    end generate;
    zero <= not zero_sig(32);                      -- Sinaliza se o resultado é zero (se zero_sig(32) for '0', zero é '1', caso contrário, zero é '0')
end TypeArchitecture;

// VHDL entity ALU_Control, as the project stores it:
library IEEE;
use IEEE.STD_LOGIC_1164.ALL;

entity ALU_Control is
    port(
        Funct    : IN std_logic_vector(3 downto 0);    -- Entrada de códigos de função da ALU (4 bits)
        AluOp   : IN std_logic_vector(1 downto 0);      -- Entrada de códigos de operação da ALU (2 bits)
        Control : OUT std_logic_vector(3 downto 0)      -- Saída do controle da ALU (4 bits)
        );
end ALU_Control;

architecture TypeArchitecture of ALU_Control is
begin

	control <= "0010" when AluOp = "00" else -- Se AluOp for "00", Control recebe "0010" (Operação: Soma)
			 "0110" when AluOp = "01" else -- Se AluOp for "01", Control recebe "0110" (Operação: Branch)
			 "0010" when Funct = "0000" else -- Se Funct for "0000", Control recebe "0010" (Operação: Adição)
			 "0110" when Funct = "1000" else -- Se Funct for "1000", Control recebe "0110" (Operação: Subtração)
			 "0011" when Funct = "0001" else -- Se Funct for "0001", Control recebe "0011" (Operação: Shift Left)
			 "0101" when Funct = "0100" else -- Se Funct for "0100", Control recebe "0101" (Operação: XOR)
			 "0111" when Funct = "0101" else -- Se Funct for "0101", Control recebe "0111" (Operação: Shift Right)
			 "0001" when Funct = "0110" else -- Se Funct for "0110", Control recebe "0001" (Operação: OR)
			 "0000" when Funct = "0111"; -- Se Funct for "0111", Control recebe "0000" (Operação: AND)
	 
end TypeArchitecture;

// VHDL entity Control_Unit, as the project stores it:
library IEEE;
use IEEE.STD_LOGIC_1164.ALL;

entity Control_Unit is
    port(
        opcode                     : IN  std_logic_vector(6 downto 0);   -- Entrada do código de operação (7 bits)
        AluSrc, reg_zero, RegWrite : OUT std_logic;                      -- Saída de sinais de controle individuais (1 bit cada)
        MemRead, MemWrite, Branch  : OUT std_logic;                      -- Saída de sinais de controle individuais (1 bit cada)
        BranchNotEq, BranchIncond  : OUT std_logic;                      -- Saída de sinais de controle individuais (1 bit cada)
        regToPC                    : OUT std_logic;                      -- Saída de sinal de controle (1 bit)
        AluOp, regSrc              : OUT std_logic_vector(1 downto 0)    -- Saída de códigos de operação da ALU e seleção de registradores (2 bits cada)
        );
end Control_Unit;

architecture TypeArchitecture of Control_Unit is
begin
    -- Processo que verifica o opcode e define os sinais de controle correspondentes
    process(opcode)
    begin
        IF (opcode = "0110011") THEN -- R-Type sem imediato (add, sub, and, or, xor, slt)
            AluSrc      <= '0';  -- Seleção de fonte para a ALU (0: A_i, 1: Immediato)
            reg_zero    <= '0';  -- Seleção de origem do registrador A (0: rs1, 1: zero)
            RegWrite    <= '1';  -- Habilita escrita no registrador destino
            MemRead     <= '0';  -- Habilita leitura de memória
            MemWrite    <= '0';  -- Habilita escrita na memória
            Branch      <= '0';  -- Habilita desvio condicional
            AluOp       <= "10"; -- Código de operação da ALU para R-Type (00: and, 01: or, 10: add, 11: sub)
            regSrc      <= "00"; -- Seleção de registradores para R-Type (00: rs1, 01: rs2, 10: rd, 11: zero)
            BranchNotEq <= '0';  -- Habilita desvio condicional se as entradas forem diferentes
            BranchIncond    <= '0';  -- Habilita desvio incondicional
            regToPC     <= '0';  -- Seleção de registrador para atualizar o PC (0: PC+4, 1: rd)
        END IF;

        IF (opcode = "0010011") THEN -- I-Type (addi, andi, ori, xori, slti)
            AluSrc      <= '1';  -- Seleção de fonte para a ALU (0: A_i, 1: Immediato)
            reg_zero      <= '0';  -- Seleção de origem do registrador A (0: rs1, 1: zero)
            RegWrite    <= '1';  -- Habilita escrita no registrador destino
            MemRead     <= '0';  -- Habilita leitura de memória
            MemWrite    <= '0';  -- Habilita escrita na memória
            Branch      <= '0';  -- Habilita desvio condicional
            AluOp       <= "11"; -- Código de operação da ALU para I-Type (00: andi, 01: ori, 10: addi, 11: slti)
            regSrc      <= "00"; -- Seleção de registradores para I-Type (00: rs1, 01: rd, 10: zero)
            BranchNotEq <= '0';  -- Habilita desvio condicional se as entradas forem diferentes
            BranchIncond    <= '0';  -- Habilita desvio incondicional
            regToPC     <= '0';  -- Seleção de registrador para atualizar o PC (0: PC+4, 1: rd)
        END IF;

        IF (opcode = "0100011") THEN -- S-Type (sw)
            AluSrc      <= '1';  -- Seleção de fonte para a ALU (0: A_i, 1: Immediato)
            reg_zero      <= '0';  -- Seleção de origem do registrador A (0: rs1, 1: zero)
            RegWrite    <= '0';  -- Habilita escrita no registrador destino
            MemRead     <= '0';  -- Habilita leitura de memória
            MemWrite    <= '1';  -- Habilita escrita na memória
            Branch      <= '0';  -- Habilita desvio condicional
            AluOp       <= "00"; -- Código de operação da ALU para S-Type (00: add)
            regSrc      <= "00"; -- Seleção de registradores para S-Type (00: rs1, 01: zero)
            BranchNotEq <= '0';  -- Habilita desvio condicional se as entradas forem diferentes
            BranchIncond    <= '0';  -- Habilita desvio incondicional
            regToPC     <= '0';  -- Seleção de registrador para atualizar o PC (0: PC+4, 1: rd)
        END IF;

        IF (opcode = "1100111") THEN -- SB-Type (beq)
            AluSrc      <= '0';  -- Seleção de fonte para a ALU (0: A_i, 1: Immediato)
            reg_zero      <= '0';  -- Seleção de origem do registrador A (0: rs1, 1: zero)
            RegWrite    <= '0';  -- Habilita escrita no registrador destino
            MemRead     <= '0';  -- Habilita leitura de memória
            MemWrite    <= '0';  -- Habilita escrita na memória
            Branch      <= '1';  -- Habilita desvio condicional
            AluOp       <= "01"; -- Código de operação da ALU para SB-Type (01: sub)
            regSrc      <= "00"; -- Seleção de registradores para SB-Type (00: rs1, 01: rs2)
            BranchNotEq <= '0';  -- Habilita desvio condicional se as entradas forem diferentes
            BranchIncond    <= '0';  -- Habilita desvio incondicional
            regToPC     <= '0';  -- Seleção de registrador para atualizar o PC (0: PC+4, 1: rd)
        END IF;

        IF (opcode = "1100011") THEN -- SB-Type (bne)
            AluSrc      <=

// VHDL entity ImmGen, as the project stores it:
library IEEE;
use IEEE.STD_LOGIC_1164.ALL;
USE IEEE.NUMERIC_STD.ALL;

entity ImmGen is
    Port( 
        instruction: in std_logic_vector(31 downto 0);  -- Entrada da instrução (32 bits)
        imm: out std_logic_vector(31 downto 0)  -- Saída do valor imediato gerado (32 bits)
        );
end ImmGen;

architecture Behavioral of ImmGen is
    signal opcode       : std_logic_vector(6 downto 0);  -- Sinal para armazenar o campo opcode da instrução (7 bits)
    signal internal_imm  : std_logic_vector(31 downto 0) := "00000000000000000000000000000000";  -- Valor imediato interno inicializado com zero

begin

    opcode <= instruction(6 downto 0);  -- Extrai o campo opcode da instrução

    process(opcode)
    begin
        if (opcode = "0010011" or opcode = "1100110") then  -- Tipo I (load-immediate, jump-register)
            internal_imm(11 downto 0)  <= instruction(31 downto 20);  -- Extrai o imediato de 11 bits
            internal_imm(31 downto 12) <= (others => instruction(31));  -- Sinal extendido para os bits mais significativos
        elsif (opcode = "1110111" or opcode = "0110111") then  -- Tipo U (lui, auipc)
            internal_imm(31 downto 12) <= instruction(31 downto 12);  -- Extrai o imediato de 20 bits
        elsif (opcode = "0100011") then  -- Tipo S (store)
            internal_imm(11 downto 5)  <= instruction(31 downto 25);  -- Extrai o imediato de 7 bits (5-11)
            internal_imm(4 downto 0)   <= instruction(11 downto 7);   -- Extrai o imediato de 5 bits (0-4)
            internal_imm(31 downto 12) <= (others => instruction(31));  -- Sinal extendido para os bits mais significativos
        elsif (opcode = "1100111" or opcode = "1100011") then  -- Tipo SB (branch)
            internal_imm(12)           <= instruction(31);          -- Extrai o bit de imediato (12)
            internal_imm(11)           <= instruction(7);           -- Extrai o bit de imediato (11)
            internal_imm(10 downto 5)  <= instruction(30 downto 25);  -- Extrai o imediato de 6 bits (5-10)
            internal_imm(4 downto 1)   <= instruction(11 downto 8);   -- Extrai o imediato de 4 bits (1-4)
            internal_imm(31 downto 13) <= (others => instruction(31));  -- Sinal extendido para os bits mais significativos
        elsif (opcode = "1101111") then  -- Tipo UJ (jump)
            internal_imm(20)           <= instruction(31);          -- Extrai o bit de imediato (20)
            internal_imm(19 downto 12) <= instruction(19 downto 12);  -- Extrai o imediato de 8 bits (12-19)
            internal_imm(11)           <= instruction(20);          -- Extrai o bit de imediato (11)
            internal_imm(10 downto 1)  <= instruction(30 downto 21);  -- Extrai o imediato de 10 bits (1-10)
        end if;
    end process;

    imm <= internal_imm;  -- Define a saída como o valor imediato gerado

end Behavioral;

// VHDL entity PC2, as the project stores it:
LIBRARY ieee;
USE ieee.std_logic_1164.all;

ENTITY PC2 IS
  PORT (
    clk      : IN  std_logic;                    -- Entrada do sinal de clock
    reset    : IN  std_logic;                    -- Entrada do sinal de reset
    pc_in    : IN  std_logic_vector(31 DOWNTO 0); -- Entrada do valor atual do PC (contador de programa)
    writeEnable   : IN std_logic;               -- Entrada do sinal de habilitação de escrita no PC
    pc_out   : OUT std_logic_vector(31 DOWNTO 0)  -- Saída do valor atualizado do PC (contador de programa)
    );
END PC2;

ARCHITECTURE TypeArchitecture OF PC2 IS

BEGIN

	PROCESS (clk, reset, writeEnable)
	BEGIN
		IF (rising_edge(clk)) THEN                      -- Detecta a borda de subida do sinal de clock
			if (pc_in = "UUUUUUUUUUUUUUUUUUUUUUUUUUUUUUUU") then   -- Verifica se o valor atual do PC é desconhecido (não inicializado)
				pc_out <= (others => '0');               -- Se for desconhecido, zera o valor do PC
			elsif (writeEnable = '0') then              -- Verifica se o sinal de habilitação de escrita está desabilitado
				pc_out <= pc_in;                         -- Se estiver desabilitado, o PC mantém o valor atual (não ocorre atualização)
			end if;
		END IF;
		IF (reset = '1') THEN                           -- Detecta a ocorrência de um reset (sinal de reset em nível alto)
			pc_out <= (others => '0');                   -- Nesse caso, zera o valor do PC
		END IF;
	END PROCESS;

END TypeArchitecture;

// VHDL entity somador, as the project stores it:
LIBRARY ieee;
USE ieee.std_logic_1164.all;

USE IEEE.std_logic_unsigned.ALL; -- Pacote para operações aritméticas com std_logic_vector

ENTITY somador IS
  PORT (
    A, B        : IN  std_logic_vector(31 DOWNTO 0); -- Vetor de entrada exemplo A e B de 32 bits
    Z           : OUT std_logic_vector(31 DOWNTO 0)  -- Vetor de saída exemplo Z de 32 bits
    );
END somador;

ARCHITECTURE TypeArchitecture OF somador IS

BEGIN

Z <= A + B; -- Saída Z é a soma dos vetores de entrada A e B

END TypeArchitecture;

// VHDL entity register_file, as the project stores it:
library ieee;
use ieee.std_logic_1164.all;
use ieee.numeric_std.all;

entity register_file is
  port(
    regA_data           : out std_logic_vector(31 downto 0);    -- Saída A do registrador
    regB_data           : out std_logic_vector(31 downto 0);    -- Saída B do registrador
    input               : in  std_logic_vector(31 downto 0);    -- Entrada de dado para escrita no registrador
    regManual_selector  : in  std_logic_vector(4 downto 0);     -- Seleção manual de um registrador de saída
    RegManual_data      : out std_logic_vector(31 downto 0);    -- Saída do registrador selecionado manualmente
    writeEnable         : in  std_logic;                        -- Sinal de habilitação de escrita no registrador
    regA_selector       : in  std_logic_vector(4 downto 0);     -- Seleção do registrador A para leitura
    regB_selector       : in  std_logic_vector(4 downto 0);     -- Seleção do registrador B para leitura
    writeReg_selector   : in  std_logic_vector(4 downto 0);     -- Seleção do registrador para escrita
    clk                 : in  std_logic                        -- Sinal de clock
    );
end register_file;

architecture TypeArchitecture of register_file is
  type registerFile is array(0 to 31) of std_logic_vector(31 downto 0);
  signal registers : registerFile := 
   -- Valores iniciais dos registradores
   -- Os primeiros 32 registradores têm os valores pré-definidos como "00000000000000000000000000010000", "00000000000000000000000000000001", etc.
   -- Até o último registrador "00000000000000000000000000000000"
   ("00000000000000000000000000010000","00000000000000000000000000000001","00000000000000000000000000000000","00000000000000000000000000000000",
    "00000000000000000000000000000000","00000000000000000000000000000000","00000000000000000000000000000000","00000000000000000000000000000000",
    "00000000000000000000000000000000","00000000000000000000000000000000","00000000000000000000000000000000","00000000000000000000000000000000",
    "00000000000000000000000000000000","00000000000000000000000000000000","00000000000000000000000000000000","00000000000000000000000000000000",
    "00000000000000000000000000000000","00000000000000000000000000000000","00000000000000000000000000000000","00000000000000000000000000000000",
    "00000000000000000000000000000000","00000000000000000000000000000000","00000000000000000000000000000000","00000000000000000000000000000000",
    "00000000000000000000000000000000","00000000000000000000000000000000","00000000000000000000000000000000","00000000000000000000000000000000",
    "00000000000000000000000000000000","00000000000000000000000000000000","00000000000000000000000000000000","00000000000000000000000000000000");

begin
  regFile : process (clk) is
  begin
    if rising_edge(clk) then
      -- Read A and B before bypass
      -- Leitura dos registradores A e B antes do bypass
      if (registers(to_integer(unsigned(regA_selector))) = "UUUUUUUUUUUUUUUUUUUUUUUUUUUUUUUU") THEN
      	regA_data <= (others => '0');  -- Se o valor for "UUUU..." (indeterminado), a saída A será "0000..."
      ELSE 
      	regA_data <= registers(to_integer(unsigned(regA_selector)));  -- Caso contrário, a saída A será o valor do registrador selecionado
      END IF;
      IF (registers(to_integer(unsigned(regB_selector))) = "UUUUUUUUUUUUUUUUUUUUUUUUUUUUUUUU") THEN
      	regB_data <= (others => '0');  -- Se o valor for "UUUU..." (indeterminado), a saída B será "0000..."
      ELSE
      	regB_data <= registers(to_integer(unsigned(regB_selector)));  -- Caso contrário, a saída B será o valor do registrador selecionado
      END IF;
      -- Write and bypass
      -- Escrita e bypass
      if writeEnable = '1' then
        registers(to_integer(unsigned(writeReg_selector))) <= input;  -- Escreve o valor da entrada no registrador selecionado
        if regA_selector = writeReg_selector then  -- Bypass para leitura A
          regA_data <= input;  -- Se o registrador A é o mesmo selecionado para escrita, a saída A recebe o valor da entrada
        end if;
        if regB_selector = writeReg_selector then  -- Bypass para leitura B
          regB_data <= input;  -- Se o registrador B é o mesmo selecionado para escrita, a saída B recebe o valor da entrada
        end if;
      end if;
    end if;
  end process;

  -- seleção manual
  -- O valor de saída RegManual_data recebe o valor do registrador selecionado manualmente (regManual_selector)
  RegManual_data <= registers(to_integer(unsigned(regManual_selector)));
  
end TypeArchitecture;

// VHDL entity IFID, as the project stores it:
LIBRARY ieee;
USE ieee.std_logic_1164.all;

ENTITY IFID IS
  PORT (
    clk         : IN  std_logic;                    -- Entrada do sinal de clock
    PC_in        : IN  std_logic_vector(31 DOWNTO 0); -- Entrada do valor atual do PC (contador de programa)
    PC_plus4_in	 : IN  std_logic_vector(31 downto 0); -- Entrada do valor do PC mais 4 (próxima instrução)
    writeEnable   : IN std_logic;                 -- Entrada do sinal de habilitação de escrita no IFID
    instruction_In      : IN  std_logic_vector(31 DOWNTO 0); -- Entrada da instrução atual buscada na memória de instruções
    PC_out       : OUT std_logic_vector(31 DOWNTO 0); -- Saída do valor atual do PC (contador de programa)
    PC_plus4_out	 : OUT std_logic_vector(31 downto 0); -- Saída do valor do PC mais 4 (próxima instrução)
    instruction_Out     : OUT std_logic_vector(31 DOWNTO 0)  -- Saída da instrução atual buscada na memória de instruções
    );
END IFID;


ARCHITECTURE TypeArchitecture OF IFID IS

SIGNAL IDIF : std_logic_vector(95 DOWNTO 0);  -- Registrador de 96 bits para armazenar os valores do IFID

BEGIN
	
	PROCESS (clk, writeEnable)
	BEGIN
		IF (rising_edge(clk)) THEN                   -- Detecta a borda de subida do sinal de clock
			if (writeEnable = '0') then             -- Verifica se o sinal de habilitação de escrita está desabilitado
				IDIF(31 DOWNTO 0) <= instruction_In;         -- Se estiver desabilitado, armazena a instrução atual no IFID
				IDIF(63 DOWNTO 32) <= PC_in;          -- Armazena o valor atual do PC
				IDIF(95 downto 64) <= PC_plus4_in;       -- Armazena o valor do PC mais 4 (próxima instrução)
			end if;
		END IF;
		IF (falling_edge(clk)) THEN                 -- Detecta a borda de descida do sinal de clock
			PC_out <= IDIF(63 DOWNTO 32);           -- Na borda de descida, coloca na saída o valor do PC atual
			instruction_Out <= IDIF(31 DOWNTO 0);          -- Coloca na saída a instrução armazenada no IFID
			PC_plus4_out <= IDIF(95 downto 64);        -- Coloca na saída o valor do PC mais 4
		END IF;
	END PROCESS;

	
END TypeArchitecture;

// VHDL entity IDEX, as the project stores it:
LIBRARY ieee;
USE ieee.std_logic_1164.all;

ENTITY IDEX IS
  PORT (
    clk            : IN  std_logic;                    -- Entrada do sinal de clock
    PC_in           : IN  std_logic_vector(31 DOWNTO 0); -- Entrada do valor atual do PC (contador de programa)
    read1_in        : IN  std_logic_vector(31 DOWNTO 0); -- Entrada do valor lido do registrador 1
    read2_in        : IN  std_logic_vector(31 DOWNTO 0); -- Entrada do valor lido do registrador 2
    immGen_in       : in  std_logic_vector(31 DOWNTO 0); -- Entrada do valor gerado pela unidade ImmGen
    aluControl_in   : IN  std_logic_vector(3 downto 0);  -- Entrada do controle da ALU
    WB_address_in       : IN  std_logic_vector(4 downto 0);  -- Entrada do endereço do registrador de destino para escrita
    WB_in		    : IN  std_logic_vector(2 downto 0);  -- Entrada da fonte de escrita no registrador de destino
    Memory_in 		    : IN  std_logic_vector(5 downto 0);  -- Entrada do sinal de controle de escrita na memória de dados
    EX_control_in    	    : IN  std_logic_vector(3 downto 0);  -- Entrada do sinal de controle de execução
    PC_plus4_in	    : IN  std_logic_vector(31 downto 0); -- Entrada do valor do PC mais 4 (próxima instrução)
    rs1_address_in		    : IN  std_logic_vector(4 downto 0);  -- Entrada do endereço do registrador 1
    rs2_address_in		    : IN  std_logic_vector(4 downto 0);  -- Entrada do endereço do registrador 2
                        
    PC_out          : OUT std_logic_vector(31 DOWNTO 0); -- Saída do valor atual do PC (contador de programa)
    read1_out	    : OUT std_logic_vector(31 DOWNTO 0); -- Saída do valor lido do registrador 1
    read2_out       : OUT std_logic_vector(31 DOWNTO 0); -- Saída do valor lido do registrador 2
    immGen_out      : OUT std_logic_vector(31 DOWNTO 0); -- Saída do valor gerado pela unidade ImmGen
    aluControl_out  : OUT std_logic_vector(3 downto 0);  -- Saída do controle da ALU
    WB_address_out       : OUT std_logic_vector(4 downto 0);  -- Saída do endereço do registrador de destino para escrita
    WB_out		    : OUT std_logic_vector(2 downto 0);  -- Saída da fonte de escrita no registrador de destino
    Memory_out 		    : OUT std_logic_vector(5 downto 0);  -- Saída do sinal de controle de escrita na memória de dados
    EXout    	    : OUT std_logic_vector(3 downto 0);  -- Saída do sinal de controle de execução
    PC_plus4_out	    : OUT std_logic_vector(31 downto 0); -- Saída do valor do PC mais 4 (próxima instrução)
    rs1_address_out	    : OUT std_logic_vector(4 downto 0);  -- Saída do endereço do registrador 1
    rs2_address_out	    : OUT std_logic_vector(4 downto 0)   -- Saída do endereço do registrador 2
    );
END IDEX;


ARCHITECTURE TypeArchitecture OF IDEX IS

SIGNAL idex_sig : std_logic_vector(191 DOWNTO 0);  -- Registrador de 192 bits para armazenar os valores do IDEX

BEGIN

	PROCESS (clk)
	BEGIN
		IF (rising_edge(clk)) THEN                   -- Detecta a borda de subida do sinal de clock
			idex_s(31 DOWNTO 0)    <= PC_in;          -- Armazena o valor atual do PC
			idex_s(63 DOWNTO 32)   <= read1_in;       -- Armazena o valor lido do registrador 1
			idex_s(95 DOWNTO 64)   <= read2_in;       -- Armazena o valor lido do registrador 2
			idex_s(127 DOWNTO 96)  <= immGen_in;      -- Armazena o valor gerado pela unidade ImmGen
			idex_s(131 DOWNTO 128) <= aluControl_in;  -- Armazena o controle da ALU
			idex_s(136 DOWNTO 132) <= wbAddIn;       -- Armazena o endereço do registrador de destino para escrita
			idex_s(139 downto 137) <= WB_in;          -- Armazena a fonte de escrita no registrador de destino
			idex_s(145 downto 140) <= Memory_in;           -- Armazena o sinal de controle de escrita na memória de dados
			idex_s(149 downto 146) <= EX_control_in;          -- Armazena o sinal de controle de execução
			idex_s(181 downto 150) <= PC_plus4_in;       -- Armazena o valor do PC mais 4 (próxima instrução)
			idex_s(186 downto 182) <= rs1_address_in;         -- Armazena o endereço do registrador 1
			idex_s(191 downto 187) <= rs2_address_in;         -- Armazena o endereço do registrador 2
		END IF;
		IF (falling_edge(clk)) THEN                 -- Detecta a borda de descida do sinal de clock
			PC_out    <= idex_sig(31 DOWNTO 0);        -- Na borda de descida, coloca na saída o valor do PC atual
			read1_out  <= idex_sig(63 DOWNTO 32);      -- Coloca na saída o valor lido do registrador 1
			read2_out  <= idex_sig(95 DOWNTO 64);      -- Coloca na saída o valor lido do registrador 2
			immGen_out <= idex_sig(127 DOWNTO 96);     -- Coloca na saída
			aluControl_out <= idex_sig(131 DOWNTO 128);
			WB_address_out <= idex_sig(136 DOWNTO 132);
			WB_out <= idex_sig(139 downto 137);
			Memory_out <= idex_sig(145 downto 140);
			EX_control_out <= idex_sig(149 downto 146);
			PC_plus4_out <= idex_sig(181 downto 150);
			rs1_address_out <= idex_sig(186 downto 182);
			rs2_address_out <= idex_sig(191 downto 187);
		END IF;
	END PROCESS;

	
END TypeArchitecture;

// VHDL entity EXMEM, as the project stores it:
LIBRARY ieee;
USE ieee.std_logic_1164.all;

ENTITY EXMEM IS
  PORT (
    clk                    : IN  std_logic;                    -- Entrada do sinal de clock
    Sum_address_in           : IN  std_logic_vector(31 DOWNTO 0); -- Entrada do resultado da ALU
    ALUzero_in             : IN  std_logic;                    -- Entrada do sinal de zero da ALU
    ALUresult_in        : IN  std_logic_vector(31 DOWNTO 0);  -- Entrada da operação da ALU
    read2_in               : IN  std_logic_vector(31 DOWNTO 0);  -- Entrada do valor lido do registrador 2
    WB_address_in          : IN  std_logic_vector(4 downto 0);  -- Entrada do endereço do registrador de destino para escrita
    WB_in		               : IN  std_logic_vector(2 downto 0);  -- Entrada da fonte de escrita no registrador de destino
    Memory_in 		         : IN  std_logic_vector(5 downto 0);  -- Entrada do sinal de controle de escrita na memória de dados
    PC_plus4_in	           : IN std_logic_vector(31 downto 0);  -- Entrada do valor do PC mais 4 (próxima instrução)
    
    PC_out                 : OUT std_logic_vector(31 DOWNTO 0); -- Saída do valor atual do PC (contador de programa)
    ALUzero_out	           : OUT std_logic;                    -- Saída do sinal de zero da ALU
    ALUresult_out       : OUT std_logic_vector(31 DOWNTO 0);  -- Saída do resultado da ALU
    read2_out              : OUT std_logic_vector(31 DOWNTO 0); -- Saída do valor lido do registrador 2
    WB_address_out         : OUT std_logic_vector(4 downto 0);  -- Saída do endereço do registrador de destino para escrita
    WB_out		             : OUT std_logic_vector(2 downto 0);  -- Saída da fonte de escrita no registrador de destino
    Memory_out 		         : OUT std_logic_vector(5 downto 0);  -- Saída do sinal de controle de escrita na memória de dados
    PC_plus4_out	         : OUT std_logic_vector(31 downto 0)  -- Saída do valor do PC mais 4 (próxima instrução)
    );
END EXMEM;


ARCHITECTURE TypeArchitecture OF EXMEM IS

SIGNAL exmem_sig : std_logic_vector(142 DOWNTO 0);  -- Registrador de 143 bits para armazenar os valores do EXMEM

BEGIN

	PROCESS (clk)
	BEGIN
		IF (rising_edge(clk)) THEN                    -- Detecta a borda de subida do sinal de clock
			exmem_sig(31 DOWNTO 0)   <= Sum_address_in;          -- Armazena o resultado da ALU
			exmem_sig(32)  <= ALUzero_in;                   -- Armazena o sinal de zero da ALU
			exmem_sig(64 DOWNTO 33)  <= ALUresult_in;          -- Armazena a operação da ALU
			exmem_sig(96 DOWNTO 65) <= read2_in;         -- Armazena o valor lido do registrador 2
			exmem_sig(101 DOWNTO 97) <= wbAddIn;        -- Armazena o endereço do registrador de destino para escrita
			exmem_sig(104 DOWNTO 102) <= WB_in;          -- Armazena a fonte de escrita no registrador de destino
			exmem_sig(110 DOWNTO 105) <= Memory_in;           -- Armazena o sinal de controle de escrita na memória de dados
			exmem_sig(142 downto 111) <= PC_plus4_in;       -- Armazena o valor do PC mais 4 (próxima instrução)
		END IF;
		IF (falling_edge(clk)) THEN                  -- Detecta a borda de descida do sinal de clock
			PC_out    <=  exmem_sig(31 DOWNTO 0);       -- Na borda de descida, coloca na saída o valor do PC atual
			ALUzero_out  <=  exmem_sig(32);                -- Coloca na saída o sinal de zero da ALU
			ALUresult_out   <=  exmem_sig(64 DOWNTO 33);       -- Coloca na saída o resultado da ALU
			read2_out <=  exmem_sig(96 DOWNTO 65);       -- Coloca na saída o valor lido do registrador 2
			WB_address_out <=  exmem_sig(101 DOWNTO 97);      -- Coloca na saída o endereço do registrador de destino para escrita
			WB_out    <=  exmem_sig(104 DOWNTO 102);     -- Coloca na saída a fonte de escrita no registrador de destino
			Memory_out     <=  exmem_sig(110 DOWNTO 105);     -- Coloca na saída o sinal de controle de escrita na memória de dados
			PC_plus4_out <=  exmem_sig(142 downto 111);     -- Coloca na saída o valor do PC mais 4 (próxima instrução)
		END IF;
	END PROCESS;

	
END TypeArchitecture;

// VHDL entity MEMWB, as the project stores it:
LIBRARY ieee;
USE ieee.std_logic_1164.all;

ENTITY MEMWB IS
  PORT (
    clk            : IN  std_logic;                    -- Entrada do sinal de clock
    mem_read_in         : IN  std_logic_vector(31 DOWNTO 0); -- Entrada do valor lido da memória ou resultado da ALU
    ALUresult_in          : IN  std_logic_vector(31 DOWNTO 0); -- Entrada do resultado da operação da ALU
    WB_address_in       : IN  std_logic_vector(4 downto 0);  -- Entrada do endereço do registrador de destino para escrita
    WB_in		    : IN  std_logic_vector(2 downto 0);  -- Entrada da fonte de escrita no registrador de destino
    PC_plus4_in	    : IN std_logic_vector(31 downto 0); -- Entrada do valor do PC mais 4 (próxima instrução)
    PC_plusAddress_in	    : IN std_logic_vector(31 downto 0); -- Entrada do valor do PC mais I (endereço de retorno para chamadas de função)
                        
    mem_read_out        : OUT std_logic_vector(31 DOWNTO 0); -- Saída do valor lido da memória ou resultado da ALU
    ALUresult_out	        : OUT std_logic_vector(31 DOWNTO 0); -- Saída do resultado da operação da ALU
    WB_address_out       : OUT std_logic_vector(4 downto 0);  -- Saída do endereço do registrador de destino para escrita
    WB_out		    : OUT std_logic_vector(2 downto 0);  -- Saída da fonte de escrita no registrador de destino
    PC_plus4_out       : OUT std_logic_vector(31 downto 0); -- Saída do valor do PC mais 4 (próxima instrução)
    PC_plusAddress_out	    : OUT std_logic_vector(31 downto 0)  -- Saída do valor do PC mais I (endereço de retorno para chamadas de função)
    );
END MEMWB;

ARCHITECTURE TypeArchitecture OF MEMWB IS

SIGNAL memwb_sig : std_logic_vector(135 DOWNTO 0);  -- Registrador de 136 bits para armazenar os valores do MEMWB

BEGIN

	PROCESS (clk)
	BEGIN
		IF (rising_edge(clk)) THEN                       -- Detecta a borda de subida do sinal de clock
			memwb_sig(31 DOWNTO 0)   <= mem_read_in;            -- Armazena o valor lido da memória ou resultado da ALU
			memwb_sig(63 DOWNTO 32)  <= ALUresult_in;             -- Armazena o resultado da operação da ALU
			memwb_sig(68 DOWNTO 64)  <= wbAddIn;           -- Armazena o endereço do registrador de destino para escrita
			memwb_sig(71 DOWNTO 69)  <= WB_in;              -- Armazena a fonte de escrita no registrador de destino
			memwb_sig(103 downto 72) <= PC_plus4_in;           -- Armazena o valor do PC mais 4 (próxima instrução)
			memwb_sig(135 downto 104) <= PC_plusAddress_in;          -- Armazena o valor do PC mais I (endereço de retorno para chamadas de função)
			
		END IF;
		IF (falling_edge(clk)) THEN                      -- Detecta a borda de descida do sinal de clock
			readOut    <=  memwb_sig(31 DOWNTO 0);         -- Na borda de descida, coloca na saída o valor lido da memória ou resultado da ALU
			ALUresult_out     <=  memwb_sig(63 DOWNTO 32);        -- Coloca na saída o resultado da operação da ALU
			WB_address_out   <=  memwb_sig(68 DOWNTO 64);        -- Coloca na saída o endereço do registrador de destino para escrita
			WB_out      <=  memwb_sig(71 DOWNTO 69);        -- Coloca na saída a fonte de escrita no registrador de destino
			PC_plus4_out   <=  memwb_sig(103 downto 72);       -- Coloca na saída o valor do PC mais 4 (próxima instrução)
			PC_plusAddress_out   <=  memwb_sig(135 downto 104);      -- Coloca na saída o valor do PC mais I (endereço de retorno para chamadas de função)
		END IF;
	END PROCESS;

	
END TypeArchitecture;

// VHDL entity Harzard, as the project stores it:
library IEEE;
use IEEE.STD_LOGIC_1164.ALL;

entity Harzard is 
	port( 
        clk 		   : IN std_logic;                          -- Entrada do sinal de clock
        MemReadSignal_EX 	   : IN std_logic;                          -- Sinal indicando leitura na memória (saída do estágio EX do pipeline)
        RegRD_EX, RegRs1, RegRs2 : IN std_logic_vector(4 downto 0);  -- Registradores de destino e fontes da instrução (saídas do estágio EX do pipeline)
        stall		   : OUT std_logic                         -- Saída que indica se um "stall" (atraso) deve ser aplicado
	);
end Harzard;

architecture TypeArchitecture of Harzard is
	signal internal_stall : std_logic := '0';  -- Sinal interno que armazena o valor do stall

begin
	process(clk)
    begin
        if ((MemReadSignal_EX = '1') and ((RegRD_EX = RegRs1) or (RegRD_EX = RegRs2))) then
            internal_stall <='1';  -- Se houver uma leitura na memória (MemReadSignal_EX = '1') e o resultado da EX estiver em RegRs1 ou RegRs2, aplica um stall
        end if;
    end process;
    stall <= internal_stall;  -- Atribui o valor do sinal interno internal_stall à saída stall
end TypeArchitecture;

// VHDL entity Forward, as the project stores it:
library IEEE;
use IEEE.STD_LOGIC_1164.ALL;

entity Forward is 
	port( 
	     clk					: IN std_logic;                      -- Entrada do sinal de clock
	     regWriteSignal_WB, regWriteMEM 	: IN std_logic;                      -- Sinais de escrita no registrador (saídas de MEM/WB e WB do pipeline)
	     RegRs1, RegRs2			: IN std_logic_vector(4 downto 0);   -- Registradores fonte da instrução (saídas de ID/EX do pipeline)
	     RegRD_WB, RegRD_MEM			: IN std_logic_vector(4 downto 0);   -- Registradores de destino (saídas de MEM/WB e EX/MEM do pipeline)
	     forwardA, forwardB		: OUT std_logic_vector(1 downto 0)   -- Saídas indicando os encaminhamentos para as fontes A e B
     );
end Forward;

architecture TypeArchitecture of Forward is
	signal internal_forwardA, internal_forwardB : std_logic_vector(1 downto 0) := "00";   -- Sinais internos que armazenam o encaminhamento

begin
	process(clk)
    begin
        if ((regWriteMEM = '1') and (not(RegRD_MEM = "00000")) and (RegRD_MEM = RegRs1)) then
        	internal_forwardA <= "10";   -- Encaminha o valor do registrador de MEM/WB para a fonte A
        end if;

        if ((regWriteMEM = '1') and (not(RegRD_MEM = "00000")) and (RegRD_MEM = RegRs2)) then
        	internal_forwardB <= "10";   -- Encaminha o valor do registrador de MEM/WB para a fonte B
        end if;

        if ((regWriteSignal_WB = '1') and (not(RegRD_WB = "00000")) and (RegRD_WB = RegRs1)) then
        	internal_forwardA <= "01";   -- Encaminha o valor do registrador de WB para a fonte A
        end if;

        if ((regWriteSignal_WB = '1') and (not(RegRD_WB = "00000")) and (RegRD_WB = RegRs2)) then
        	internal_forwardB <= "01";   -- Encaminha o valor do registrador de WB para a fonte B
        end if;

    end process;

    forwardA <= internal_forwardA;   -- Atribui o valor do sinal interno internal_forwardA à saída forwardA
    forwardB <= internal_forwardB;   -- Atribui o valor do sinal interno internal_forwardB à saída forwardB
end TypeArchitecture;
