// Logisim project CPU_vetorial_p2.circ as structural Verilog
module main (
  input  [4:0] in_1,
  input  in_2
);

  wire alu_1_zero, and_1_out, clock_1_out, d_ff_1_q, exmem_1_aluzero_out, multiplexer_5_out, not_1_out,
       or_2_out;
  wire [1:0] control_unit_1_aluop, control_unit_1_regsrc, control_unit_1_vecsize, or_1_out;
  wire [2:0] exmem_1_wb_out, idex_1_wb_out, memwb_1_wb_out;
  wire [2:2] control_unit_1_regwrite;
  wire [3:0] alu_control_1_control, idex_1_alucontrol_out, ifid_1_instruction_out_6;
  wire [4:0] control_unit_1_alusrc, exmem_1_memory_out, exmem_1_wb_address_out, idex_1_wb_address_out,
       ifid_1_instruction_out_3, ifid_1_instruction_out_4, ifid_1_instruction_out_5, memwb_1_wb_address_out;
  wire [5:0] control_unit_1_memread, idex_1_memory_out;
  wire [6:0] idex_1_ex_control_out, ifid_1_instruction_out_2;
  wire [7:0] counter_1_q;
  wire [31:0] alu_1_result, exmem_1_aluresult_out, exmem_1_pc_out, exmem_1_pc_plus4_out, exmem_1_read2_out,
       idex_1_immgen_out, idex_1_pc_out, idex_1_pc_plus4_out, idex_1_read1_out, idex_1_read2_out,
       ifid_1_pc_out, ifid_1_pc_plus4_out, immgen_1_imm, memwb_1_aluresult_out, memwb_1_mem_read_out,
       memwb_1_pc_plus4_out, memwb_1_pc_plusaddress_out, multiplexer_1_out, multiplexer_2_out,
       multiplexer_3_out, multiplexer_4_out, multiplexer_6_out, pc2_1_pc_out, ram_1_dout,
       register_file_1_rega_data, register_file_1_regb_data, register_file_1_regmanual_data, rom_1_data,
       somador_1_z, somador_2_z;
  wire [31:25] ifid_1_instruction_out;

  Clock clock_1 (.out(clock_1_out));
  Multiplexer #(.width(32)) multiplexer_1 (
    .in0(multiplexer_2_out), .in1(somador_1_z), .out(multiplexer_1_out), .sel(d_ff_1_q));
  D_Flip_Flop d_ff_1 (.D(1'b0), .clk(clock_1_out), .Q(d_ff_1_q));  // open: Qn, preset, reset
  Counter counter_1 (.Q(counter_1_q), .clk(clock_1_out), .clr(in_2));  // open: load, D, count, carry, up
  PC2 pc2_1 (.clk(counter_1_q[0]), .reset(in_2), .pc_in(multiplexer_1_out), .pc_out(pc2_1_pc_out));
  ROM #(.addrWidth(24), .dataWidth(32)) rom_1 (.addr(pc2_1_pc_out[23:0]), .data(rom_1_data));
  somador somador_1 (.A(pc2_1_pc_out), .B(32'h1), .Z(somador_1_z));
  IFID ifid_1 (
    .clk(counter_1_q[0]), .PC_in(pc2_1_pc_out), .PC_plus4_in(somador_1_z), .instruction_in(rom_1_data),
    .PC_out(ifid_1_pc_out), .PC_plus4_out(ifid_1_pc_plus4_out),
    .instruction_out({ifid_1_instruction_out[31], ifid_1_instruction_out_6[3], ifid_1_instruction_out[29:25], ifid_1_instruction_out_4, ifid_1_instruction_out_3, ifid_1_instruction_out_6[2:0], ifid_1_instruction_out_5, ifid_1_instruction_out_2}));
  // Probe on {ifid_1_instruction_out[31], ifid_1_instruction_out_6[3], ifid_1_instruction_out[29:25], ifid_1_instruction_out_4, ifid_1_instruction_out_3, ifid_1_instruction_out_6[2:0], ifid_1_instruction_out_5, ifid_1_instruction_out_2}
  // Probe on register_file_1_regmanual_data
  register_file register_file_1 (
    .\input (multiplexer_6_out), .regManual_selector(in_1), .writeEnable(memwb_1_wb_out[2]),
    .regA_selector(ifid_1_instruction_out_3), .regB_selector(ifid_1_instruction_out_4),
    .writeReg_selector(memwb_1_wb_address_out), .clk(clock_1_out), .regA_data(register_file_1_rega_data),
    .regB_data(register_file_1_regb_data), .RegManual_data(register_file_1_regmanual_data));
  ImmGen immgen_1 (
    .instruction({ifid_1_instruction_out[31], ifid_1_instruction_out_6[3], ifid_1_instruction_out[29:25], ifid_1_instruction_out_4, ifid_1_instruction_out_3, ifid_1_instruction_out_6[2:0], ifid_1_instruction_out_5, ifid_1_instruction_out_2}),
    .imm(immgen_1_imm));
  Control_Unit control_unit_1 (
    .opcode(ifid_1_instruction_out_2), .AluSrc(control_unit_1_alusrc[0]),
    .reg_zero(control_unit_1_alusrc[1]), .RegWrite(control_unit_1_regwrite[2]),
    .MemRead(control_unit_1_memread[0]), .MemWrite(control_unit_1_memread[1]),
    .Branch(control_unit_1_memread[2]), .BranchNotEq(control_unit_1_memread[3]),
    .BranchIncond(control_unit_1_memread[4]), .regToPC(control_unit_1_memread[5]),
    .mode(control_unit_1_alusrc[4]), .AluOp(control_unit_1_aluop), .regSrc(control_unit_1_regsrc),
    .vecSize(control_unit_1_vecsize));
  Multiplexer #(.select(2), .width(32)) multiplexer_2 (
    .in0(somador_1_z), .in1(exmem_1_pc_out), .in2(exmem_1_aluresult_out), .in3(exmem_1_aluresult_out),
    .out(multiplexer_2_out), .sel(or_1_out));
  // Probe on immgen_1_imm
  IDEX idex_1 (
    .clk(counter_1_q[0]), .PC_in(ifid_1_pc_out), .read1_in(register_file_1_rega_data),
    .read2_in(register_file_1_regb_data), .immGen_in(immgen_1_imm), .aluControl_in(ifid_1_instruction_out_6),
    .WB_address_in(ifid_1_instruction_out_5), .WB_in({control_unit_1_regwrite[2], control_unit_1_regsrc}),
    .Memory_in(control_unit_1_memread),
    .EX_control_in({control_unit_1_vecsize, control_unit_1_alusrc[4], control_unit_1_aluop, control_unit_1_alusrc[1:0]}),
    .PC_plus4_in(ifid_1_pc_plus4_out), .PC_out(idex_1_pc_out), .read1_out(idex_1_read1_out),
    .read2_out(idex_1_read2_out), .immGen_out(idex_1_immgen_out), .aluControl_out(idex_1_alucontrol_out),
    .WB_address_out(idex_1_wb_address_out), .WB_out(idex_1_wb_out), .Memory_out(idex_1_memory_out),
    .EX_control_out(idex_1_ex_control_out), .PC_plus4_out(idex_1_pc_plus4_out));
  Multiplexer #(.width(32)) multiplexer_3 (
    .in0(idex_1_read1_out), .in1({32{1'b0}}), .out(multiplexer_3_out), .sel(idex_1_ex_control_out[1]));
  Multiplexer #(.width(32)) multiplexer_4 (
    .in0(idex_1_read2_out), .in1(idex_1_immgen_out), .out(multiplexer_4_out), .sel(idex_1_ex_control_out[0]));
  somador somador_2 (.A(idex_1_pc_out), .B(idex_1_immgen_out), .Z(somador_2_z));
  ALU alu_1 (
    .A(multiplexer_3_out), .B(multiplexer_4_out), .control(alu_control_1_control),
    .mode(idex_1_ex_control_out[4]), .vecSize(idex_1_ex_control_out[6:5]), .result(alu_1_result),
    .zero(alu_1_zero));
  ALU_Control alu_control_1 (
    .Funct(idex_1_alucontrol_out), .AluOp(idex_1_ex_control_out[3:2]), .Control(alu_control_1_control));
  EXMEM exmem_1 (
    .clk(counter_1_q[0]),
    .ALUresult_in({somador_2_z[31], alu_1_result[31], somador_2_z[30], alu_1_result[30], somador_2_z[29], alu_1_result[29], somador_2_z[28], alu_1_result[28], somador_2_z[27], alu_1_result[27], somador_2_z[26], alu_1_result[26], somador_2_z[25], alu_1_result[25], somador_2_z[24], alu_1_result[24], somador_2_z[23], alu_1_result[23], somador_2_z[22], alu_1_result[22], somador_2_z[21], alu_1_result[21], somador_2_z[20], alu_1_result[20], somador_2_z[19], alu_1_result[19], somador_2_z[18], alu_1_result[18], somador_2_z[17], alu_1_result[17], somador_2_z[16], alu_1_result[16], somador_2_z[15], alu_1_result[15], somador_2_z[14], alu_1_result[14], somador_2_z[13], alu_1_result[13], somador_2_z[12], alu_1_result[12], somador_2_z[11], alu_1_result[11], somador_2_z[10], alu_1_result[10], somador_2_z[9], alu_1_result[9], somador_2_z[8], alu_1_result[8], somador_2_z[7], alu_1_result[7], somador_2_z[6], alu_1_result[6], somador_2_z[5], alu_1_result[5], somador_2_z[4], alu_1_result[4], somador_2_z[3], alu_1_result[3], somador_2_z[2], alu_1_result[2], somador_2_z[1], alu_1_result[1], somador_2_z[0], alu_1_result[0]}),
    .ALUzero_in(alu_1_zero), .read2_in(idex_1_read2_out), .WB_address_in(idex_1_wb_address_out),
    .WB_in(idex_1_wb_out), .Memory_in(idex_1_memory_out), .PC_plus4_in(idex_1_pc_plus4_out),
    .PC_out(exmem_1_pc_out), .ALUzero_out(exmem_1_aluzero_out), .ALUresult_out(exmem_1_aluresult_out),
    .read2_out(exmem_1_read2_out), .WB_address_out(exmem_1_wb_address_out), .WB_out(exmem_1_wb_out),
    .Memory_out({or_1_out[1], exmem_1_memory_out}), .PC_plus4_out(exmem_1_pc_plus4_out));
  or or_1 (or_1_out[0], exmem_1_memory_out[4], and_1_out);
  and and_1 (and_1_out, or_2_out, multiplexer_5_out);
  or or_2 (or_2_out, exmem_1_memory_out[2], exmem_1_memory_out[3]);
  Multiplexer multiplexer_5 (
    .in0(exmem_1_aluzero_out), .in1(not_1_out), .out(multiplexer_5_out), .sel(exmem_1_memory_out[3]));
  not not_1 (not_1_out, exmem_1_aluzero_out);
  RAM #(.addrWidth(24), .dataWidth(32)) ram_1 (
    .addr(exmem_1_aluresult_out[23:0]), .we(exmem_1_memory_out[1]), .oe(exmem_1_memory_out[0]),
    .clk(clock_1_out), .din(exmem_1_read2_out), .dout(ram_1_dout));
  MEMWB memwb_1 (
    .clk(counter_1_q[0]), .mem_read_in(ram_1_dout), .ALUresult_in(exmem_1_aluresult_out),
    .WB_address_in(exmem_1_wb_address_out), .WB_in(exmem_1_wb_out), .PC_plus4_in(exmem_1_pc_plus4_out),
    .PC_plusAddress_in(exmem_1_pc_out), .mem_read_out(memwb_1_mem_read_out),
    .ALUresult_out(memwb_1_aluresult_out), .WB_address_out(memwb_1_wb_address_out), .WB_out(memwb_1_wb_out),
    .PC_plus4_out(memwb_1_pc_plus4_out), .PC_plusAddress_out(memwb_1_pc_plusaddress_out));
  Multiplexer #(.select(2), .width(32)) multiplexer_6 (
    .in0(memwb_1_aluresult_out), .in1(memwb_1_mem_read_out), .in2(memwb_1_pc_plus4_out),
    .in3(memwb_1_pc_plusaddress_out), .out(multiplexer_6_out), .sel(memwb_1_wb_out[1:0]));

  // Notes on the sheet:
  //   contents of rom_1 (hex, n*v repeats v):
  //   100180
endmodule

// VHDL entity ALU, as the project stores it:
library IEEE;
use IEEE.STD_LOGIC_1164.ALL;
use ieee.numeric_std.ALL;
USE IEEE.std_logic_unsigned.ALL;

entity ALU is
    port(
    A, B       : in std_logic_vector(31 downto 0);   -- Entradas A e B de 32 bits
    control   : in std_logic_vector(3 downto 0);    -- Sinal de controle de 4 bits para selecionar a operação
    mode      : in std_logic;                       -- Modo de operação: 0 para operação única e 1 para operação vetorial
    vecSize   : in std_logic_vector(1 downto 0);    -- Tamanho do vetor de operações (usado no modo vetorial)
    result    : out std_logic_vector(31 downto 0);  -- Saída da operação única (modo 0)
    zero      : out std_logic                       -- Sinal de saída indicando se o resultado é zero
    );
end ALU;

architecture TypeArchitecture of ALU is

-- Declaração dos sinais internos da ALU
signal zero_out   : std_logic_vector(32 downto 0);
signal zero_vec   : std_logic_vector(32 downto 0);
signal result_out : std_logic_vector(31 downto 0);
signal result_vec : std_logic_vector(31 downto 0);
signal add_vec    : std_logic_vector(31 downto 0);
signal sub_vec    : std_logic_vector(31 downto 0);
signal shiftl_vec : std_logic_vector(31 downto 0);
signal shiftr_vec : std_logic_vector(31 downto 0);

signal A3116 	   : std_logic_vector(15 downto 0);
signal A1500 	   : std_logic_vector(15 downto 0);

signal A3124      : std_logic_vector(7 downto 0);
signal A2316      : std_logic_vector(7 downto 0);
signal A1508      : std_logic_vector(7 downto 0);
signal A0700      : std_logic_vector(7 downto 0);

signal A3128      : std_logic_vector(3 downto 0);
signal A2724      : std_logic_vector(3 downto 0);
signal A2320      : std_logic_vector(3 downto 0);
signal A1916      : std_logic_vector(3 downto 0);
signal A1512      : std_logic_vector(3 downto 0);
signal A1108      : std_logic_vector(3 downto 0);
signal A0704      : std_logic_vector(3 downto 0);
signal A0300      : std_logic_vector(3 downto 0);

signal intB       : integer;

begin

	-- Conversão da entrada B para inteiro para uso nas operações de deslocamento
	intB <= to_integer(unsigned(B));

	-- Divisão do sinal de entrada A para partes menores para cálculos vetoriais
	A3116 <= A(31 downto 16);
	A1500 <= A(15 downto 0);

	A3124 <= A(31 downto 24);
	A2316 <= A(23 downto 16);
	A1508 <= A(15 downto 8);
	A0700 <= A(7 downto 0);

	A3128 <= A(31 downto 28);
	A2724 <= A(27 downto 24);
	A2320 <= A(23 downto 20);
	A1916 <= A(19 downto 16);
	A1512 <= A(15 downto 12);
	A1108 <= A(11 downto 8);
	A0704 <= A(7 downto 4);
	A0300 <= A(3 downto 0);
	
	-- Cálculos das operações vetoriais com base no tamanho do vetor (vecSize)
	add_vec <= (A + B) when vecSize = "11" else
			 ((A3116 + B(31 downto 16)) & (A1500 + B(15 downto 0))) when vecSize = "10" else
			 ((A3124 + B(31 downto 24)) & (A2316 + B(23 downto 16)) & (A1508 + B(15 downto 8)) & (A0700 + B(7 downto 0))) when vecSize = "01" else
			 ((A3128 + B(31 downto 28)) & (A2724 + B(27 downto 24)) & (A2320 + B(23 downto 20)) & (A1916 + B(19 downto 16)) & (A1512 + B(15 downto 12)) & (A1108 + B(11 downto 8)) & (A0704 + B(7 downto 4)) & (A0300 + B(3 downto 0))) when vecSize = "00";
	
	sub_vec <= (A - B) when vecSize = "11" else
			 ((A3116 - B(31 downto 16)) & (A1500 - B(15 downto 0))) when vecSize = "10" else
			 ((A3124 - B(31 downto 24)) & (A2316 - B(23 downto 16)) & (A1508 - B(15 downto 8)) & (A0700 - B(7 downto 0))) when vecSize = "01" else
			 ((A3128 - B(31 downto 28)) & (A2724 - B(27 downto 24)) & (A2320 - B(23 downto 20)) & (A1916 - B(19 downto 16)) & (A1512 - B(15 downto 12)) & (A1108 - B(11 downto 8)) & (A0704 - B(7 downto 4)) & (A0300 - B(3 downto 0))) when vecSize = "00";
	
	-- Cálculos das operações de deslocamento vetoriais
	shiftl_vec <= (std_logic_vector(shift_left(unsigned(A), intB))) when vecSize = "11" else
			 ((std_logic_vector(shift_left(unsigned(A3116), intB))) & std_logic_vector(shift_left(unsigned(A1500), intB))) when vecSize = "10" else
			 ((std_logic_vector(shift_left(unsigned(A3124), intB))) & (std_logic_vector(shift_left(unsigned(A2316), intB))) & (std_logic_vector(shift_left(unsigned(A1508), intB))) & (std_logic_vector(shift_left(unsigned(A0700), intB)))) when vecSize = "01" else
			 ((std_logic_vector(shift_left(unsigned(A3128), intB))) & (std_logic_vector(shift_left(unsigned(A2724), intB))) & (std_logic_vector(shift_left(unsigned(A2320), intB))) & (std_logic_vector(shift_left(unsigned(A1916), intB))) & (std_logic_vector(shift_left(unsigned(A1512), intB))) & (std_logic_vector(shift_left(unsigned(A1108), intB))) & (std_logic_vector(shift_left(unsigned(A0704), intB))) & (std_logic_vector(shift_left(unsigned(A0300), intB)))) when vecSize = "00";

	shiftr_vec <= (std_logic_vector(shift_right(unsigned(A), intB))) when vecSize = "11" else
			 ((std_logic_vector(shift_right(unsigned(A3116), intB))) & std_logic_vector(shift_right(unsigned(A1500), intB))) when vecSize = "10" else
			 ((std_logic_vector(shift_right(unsigned(A3124), intB))) & (std_logic_vector(shift_right(unsigned(A2316), intB))) & (std_logic_vector(shift_right(unsigned(A1508), intB))) & (std_logic_vector(shift_right(unsigned(A0700), intB)))) when vecSize = "01" else
			 ((std_logic_vector(shift_right(unsigned(A3128), intB))) & (std_logic_vector(shift_right(unsigned(A2724), intB))) & (std_logic_vector(shift_right(unsigned(A2320), intB))) & (std_logic_vector(shift_right(unsigned(A1916), intB))) & (std_logic_vector(shift_right(unsigned(A1512), intB))) & (std_logic_vector(shift_right(unsigned(A1108), intB))) & (std_logic_vector(shift_right(unsigned(A0704), intB))) & (std_logic_vector(shift_right(unsigned(A0300), intB)))) when vecSize = "00";
	
	-- Seleção da operação de acordo com o sinal de controle (control)
	result_vec <= add_vec when control = "0010" else
			    sub_vec when control = "0110" else
			    shiftl_vec when control = "0011" else
			    shiftr_vec when control = "0111" else
			    (others => '0');

	-- Seleção da operação no modo único ou vetorial (modo 0 ou 1)
    result_out <= (A + B) when control = "0010" else
    			   (A - B) when control = "0110" else
    			   (A XOR B) when control = "0101" else
    			   (A OR B) when control = "0001" else
    			   (A AND B) when control = "0000" else
    			   (std_logic_vector(shift_left(unsigned(A), intB))) when control = "0011" else
    			   (std_logic_vector(shift_right(unsigned(A), intB))) when control = "0111";
        			
    result <= result_out when mode = '0' else
    		    result_vec when mode = '1';
    		    
    -- Cálculo dos sinais de saída zero para modo único e vetorial
    zero_out(0)<= '0';
    zero_vec(0) <= '0';
    G2: for I in 1 to 32 generate
            zero_out(I) <= zero_out(I - 1) or result_out(I - 1);
            zero_vec(I) <= zero_vec(I - 1) or result_vec(I - 1);
    end generate;
    zero <= (not zero_out(32)) when mode = '0' else
    		  (not zero_vec(32)) when mode = '1';
end TypeArchitecture;

// VHDL entity ALU_Control, as the project stores it:
library IEEE;
use IEEE.STD_LOGIC_1164.ALL;

entity ALU_Control is
    port(
        Funct    : IN std_logic_vector(3 downto 0);   -- Entrada que contém o código da função da ALU
        AluOp     : IN std_logic_vector(1 downto 0);   -- Entrada que contém o código da operação da ALU
        Control   : OUT std_logic_vector(3 downto 0)   -- Saída que contém o sinal de controle da ALU
        );
end ALU_Control;

architecture TypeArchitecture of ALU_Control is
begin

	-- Lógica para gerar o sinal de controle (Control) com base nas entradas Funct e AluOp
	control <= "0010" when AluOp = "00" else   -- Operação de adição
			 "0110" when AluOp = "01" else   -- Operação de subtração
			 "0010" when Funct = "0000" else -- Funct = 0000, operação de adição
			 "0110" when Funct = "1000" else -- Funct = 1000, operação de subtração
			 "0011" when Funct = "0001" else -- Funct = 0001, operação de shift left
			 "0101" when Funct = "0100" else -- Funct = 0100, operação de XOR
			 "0111" when Funct = "0101" else -- Funct = 0101, operação de shift right
			 "0001" when Funct = "0110" else -- Funct = 0110, operação de OR
			 "0000" when Funct = "0111";     -- Funct = 0111, operação de AND
			 
	-- As combinações restantes de Funct e AluOp não têm uma operação específica definida.
	-- Caso nenhuma das condições acima seja satisfeita, o sinal de controle será "0000" (AND).
	
end TypeArchitecture;

// VHDL entity Control_Unit, as the project stores it:
library IEEE;
use IEEE.STD_LOGIC_1164.ALL;

entity Control_Unit is
    port(
        opcode                     : IN  std_logic_vector(6 downto 0); -- Entrada que contém o opcode da instrução
        AluSrc, reg_zero, RegWrite 	: OUT std_logic;                   -- Sinais de controle da ALU
        MemRead, MemWrite, Branch  : OUT std_logic;                   -- Sinais de controle de memória
        BranchNotEq, BranchIncond		: OUT std_logic;                   -- Sinais de controle para desvios condicionais e incondicionais
        regToPC, mode			    : OUT std_logic;                   -- Sinais de controle para modificação do PC (Contador de Programa)
        AluOp, regSrc, vecSize		: OUT std_logic_vector(1 downto 0) -- Sinais de controle adicionais para a ALU
        );
end Control_Unit;

architecture TypeArchitecture of Control_Unit is

begin
	process(opcode)
	begin
	    -- Bloco de seleção para gerar os sinais de controle com base no opcode da instrução
	    IF (opcode = "0110011") THEN -- R-Type sem imediato
	        AluSrc      <= '0';
	        reg_zero      <= '0';
	        RegWrite    <= '1';
	        MemRead     <= '0';
	        MemWrite    <= '0';
	        Branch      <= '0';
	        AluOp       <= "10";
	        regSrc      <= "00";
	        BranchNotEq <= '0';
	        BranchIncond    <= '0';
	        regToPC     <= '0';
	        mode        <= '0';     
	        vecSize     <= "00";
	    END IF;
	    
	    -- Mais blocos IF/THEN/ELSE para mapear os demais opcodes às operações e sinais de controle correspondentes.
	    -- Cada bloco IF/THEN/ELSE representa uma instrução diferente, definindo quais sinais de controle devem ser ativados
	    -- para cada tipo de instrução.

	end process;
end TypeArchitecture;

// VHDL entity ImmGen, as the project stores it:
library IEEE;
use IEEE.STD_LOGIC_1164.ALL;
USE IEEE.NUMERIC_STD.ALL;

entity ImmGen is
    Port( 
        instruction: in std_logic_vector(31 downto 0); -- Entrada contendo a instrução de 32 bits
        imm: out std_logic_vector(31 downto 0)  -- Saída contendo o imediato de 32 bits
    );
end ImmGen;

architecture Behavioral of ImmGen is
    -- Declaração de sinais para armazenar o opcode e o imediato interno.
    signal opcode        : std_logic_vector(6 downto 0); 
    signal internal_imm   : std_logic_vector(31 downto 0) := "00000000000000000000000000000000"; -- Inicializa o imediato interno com valor '0'.

begin
    -- Extrai o opcode da instrução de entrada.
    opcode <= instruction(6 downto 0);

    process(opcode)
    begin
        -- Bloco de seleção para gerar o imediato com base no opcode da instrução
        if (opcode = "0010011" or opcode = "1100110" or opcode = "0000100" or opcode = "0000101" or opcode = "0000001") then --I type
            internal_imm(11 downto 0)  <= instruction(31 downto 20);     -- Bits 31:20 são copiados diretamente para os bits 11:0 do imediato
            internal_imm(31 downto 12) <= (others => instruction(31));  -- O bit 31 é copiado para todos os bits 31:12 do imediato
        elsif (opcode = "1110111" or opcode = "0110111" or opcode = "0001000" or opcode = "0001001" or opcode = "0001010") then -- U type
            internal_imm(31 downto 12) <= instruction(31 downto 12);    -- Bits 31:12 são copiados diretamente para os bits 31:12 do imediato
        elsif (opcode = "0100011") then -- S type
            internal_imm(11 downto 5) <= instruction(31 downto 25);     -- Bits 31:25 são copiados diretamente para os bits 11:5 do imediato
            internal_imm(4 downto 0)  <= instruction(11 downto 7);      -- Bits 11:7 são copiados diretamente para os bits 4:0 do imediato
            internal_imm(31 downto 12) <= (others => instruction(31));  -- O bit 31 é copiado para todos os bits 31:12 do imediato
        elsif (opcode = "1100111" or opcode = "1100011") then -- SB type
            internal_imm(12) <= instruction(31);                       -- O bit 31 é copiado para o bit 12 do imediato
            internal_imm(11) <= instruction(7);                        -- O bit 7 é copiado para o bit 11 do imediato
            internal_imm(10 downto 5) <= instruction(30 downto 25);     -- Bits 30:25 são copiados diretamente para os bits 10:5 do imediato
            internal_imm(4 downto 1) <= instruction(11 downto 8);       -- Bits 11:8 são copiados diretamente para os bits 4:1 do imediato
            internal_imm(31 downto 13) <= (others => instruction(31));  -- O bit 31 é copiado para todos os bits 31:13 do imediato
        elsif (opcode = "1101111") then -- UJ type
            internal_imm(20) <= instruction(31);                       -- O bit 31 é copiado para o bit 20 do imediato
            internal_imm(19 downto 12) <= instruction(19 downto 12);    -- Bits 19:12 são copiados diretamente para os bits 19:12 do imediato
            internal_imm(11) <= instruction(20);                       -- O bit 20 é copiado para o bit 11 do imediato
            internal_imm(10 downto 1) <= instruction(30 downto 21);     -- Bits 30:21 são copiados diretamente para os bits 10:1 do imediato
        end if;
    end process;

    -- Saída do imediato gerado.
    imm <= internal_imm;

end Behavioral;

// VHDL entity PC2, as the project stores it:
LIBRARY ieee;
USE ieee.std_logic_1164.all;

ENTITY PC2 IS
  PORT (
    clk      : IN  std_logic;                    -- Sinal de clock (entrada)
    reset    : IN  std_logic;                    -- Sinal de reset (entrada)
    pc_in    : IN  std_logic_vector(31 DOWNTO 0); -- Dado de entrada de 32 bits (vetor de entrada)
    pc_out   : OUT std_logic_vector(31 DOWNTO 0)  -- Dado de saída de 32 bits (vetor de saída)
  );
END PC2;

ARCHITECTURE TypeArchitecture OF PC2 IS
BEGIN
	PROCESS (clk, reset)
	BEGIN
		IF (rising_edge(clk)) THEN
			if (pc_in = "UUUUUUUUUUUUUUUUUUUUUUUUUUUUUUUU") then
				-- Se a entrada for desconhecida (U), o dado de saída é zerado.
				pc_out <= (others => '0');
			else
				-- Caso contrário, copia o dado de entrada para a saída.
				pc_out <= pc_in;
			end if;
		END IF;
		IF (reset = '1') THEN
			-- Se o sinal de reset for '1', o dado de saída é zerado.
			pc_out <= (others => '0');
		END IF;
	END PROCESS;
END TypeArchitecture;

// VHDL entity somador, as the project stores it:
LIBRARY ieee;
USE ieee.std_logic_1164.all;
USE IEEE.std_logic_unsigned.ALL;

ENTITY somador IS
  PORT (
    A, B        : IN  std_logic_vector(31 DOWNTO 0); -- Números de entrada de 32 bits (vetor de entrada)
    Z           : OUT std_logic_vector(31 DOWNTO 0)  -- Resultado da soma (vetor de saída)
  );
END somador;

ARCHITECTURE TypeArchitecture OF somador IS
BEGIN

  -- O sinal de saída Z recebe a soma dos valores de A e B.
  Z <= A + B;

END TypeArchitecture;

// VHDL entity register_file, as the project stores it:
library ieee;
use ieee.std_logic_1164.all;
use ieee.numeric_std.all;

entity register_file is
  port(
    regA_data          : out std_logic_vector(31 downto 0);  -- Saída do registro A
    regB_data          : out std_logic_vector(31 downto 0);  -- Saída do registro B
    RegManual_data     : out std_logic_vector(31 downto 0);  -- Saída de um registro selecionado manualmente
    input              : in  std_logic_vector(31 downto 0);  -- Dado de entrada para escrever em um registro
    regManual_selector : in  std_logic_vector(4 downto 0);   -- Seleção manual de registro de saída
    writeEnable        : in  std_logic;                      -- Sinal de habilitação de escrita em um registro
    regA_selector      : in  std_logic_vector(4 downto 0);   -- Seleção do registrador A para leitura
    regB_selector      : in  std_logic_vector(4 downto 0);   -- Seleção do registrador B para leitura
    writeReg_selector  : in  std_logic_vector(4 downto 0);   -- Seleção do registrador para escrita
    clk                : in  std_logic                       -- Sinal de clock
    );
end register_file;

architecture TypeArchitecture of register_file is
  -- Declaração de um tipo array que representa o banco de registradores com 32 registros de 32 bits cada
  type registerFile is array(0 to 31) of std_logic_vector(31 downto 0);
  -- Declaração de um sinal (variável interna) chamado "registers" do tipo registerFile
  signal registers : registerFile := 
   ("00000000000000000000000000011111","00000000000000000000000000000001","00000000000000000000000000000000","00000000000000000000000000000000",
    "00000000000000000000000000000000","00000000000000000000000000000000","00000000000000000000000000000000","00000000000000000000000000000000",
    "00000000000000000000000000000000","00000000000000000000000000000000","00000000000000000000000000000000","00000000000000000000000000000000",
    "00000000000000000000000000000000","00000000000000000000000000000000","00000000000000000000000000000000","00000000000000000000000000000000",
    "00000000000000000000000000000000","00000000000000000000000000000000","00000000000000000000000000000000","00000000000000000000000000000000",
    "00000000000000000000000000000000","00000000000000000000000000000000","00000000000000000000000000000000","00000000000000000000000000000000",
    "00000000000000000000000000000000","00000000000000000000000000000000","00000000000000000000000000000000","00000000000000000000000000000000",
    "00000000000000000000000000000000","00000000000000000000000000000000","00000000000000000000000000000000","00000000000000000000000000000000");
begin
  regFile : process (clk) is
  begin
    if rising_edge(clk) then
      -- Read A and B before bypass
      -- Realiza a leitura dos registradores A e B antes de fazer o bypass
      if (registers(to_integer(unsigned(regA_selector))) = "UUUUUUUUUUUUUUUUUUUUUUUUUUUUUUUU") THEN
        regA_data <= (others => '0');  -- Se o registro for inválido (contém "U"), a saída é zerada
      else 
        regA_data <= registers(to_integer(unsigned(regA_selector)));  -- Caso contrário, a saída é o valor do registrador A
      end if;
      IF (registers(to_integer(unsigned(regB_selector))) = "UUUUUUUUUUUUUUUUUUUUUUUUUUUUUUUU") THEN
        regB_data <= (others => '0');  -- Se o registro for inválido (contém "U"), a saída é zerada
      else
        regB_data <= registers(to_integer(unsigned(regB_selector)));  -- Caso contrário, a saída é o valor do registrador B
      end if;
      -- Write and bypass
      -- Escrita e bypass
      if writeEnable = '1' then
        -- Se o sinal de escrita estiver habilitado (writeEnable = '1'), então o dado de entrada "input" será escrito no registrador selecionado por "writeReg_selector"
        registers(to_integer(unsigned(writeReg_selector))) <= input;  -- Write
        -- Além disso, é feito o bypass para leitura dos registradores A e B
        if regA_selector = writeReg_selector then  -- Bypass para leitura do registrador A
          regA_data <= input;  -- O valor de "input" é direcionado para a saída do registrador A
        end if;
        if regB_selector = writeReg_selector then  -- Bypass para leitura do registrador B
          regB_data <= input;  -- O valor de "input" é direcionado para a saída do registrador B
        end if;
      end if;
    end if;
  end process;
  -- seleção manual
  -- Saída de um registrador selecionado manualmente com base no valor de "regManual_selector"
  RegManual_data <= registers(to_integer(unsigned(regManual_selector)));
end TypeArchitecture;

// VHDL entity IFID, as the project stores it:
library ieee;
use ieee.std_logic_1164.all;

ENTITY IFID IS
  PORT (
    clk                 : IN  std_logic;                    -- Sinal de clock
    PC_in               : IN  std_logic_vector(31 DOWNTO 0); -- PC de entrada (Program Counter)
    PC_plus4_in         : IN  std_logic_vector(31 DOWNTO 0); -- PC+4 de entrada (PC + 4)
    instruction_in      : IN  std_logic_vector(31 DOWNTO 0); -- Instrução de entrada
    PC_out              : OUT std_logic_vector(31 DOWNTO 0); -- PC de saída (Program Counter)
    PC_plus4_out        : OUT std_logic_vector(31 DOWNTO 0); -- PC+4 de saída (PC + 4)
    instruction_out     : OUT std_logic_vector(31 DOWNTO 0)  -- Instrução de saída
    );
END IFID;

ARCHITECTURE TypeArchitecture OF IFID IS

SIGNAL IDIF : std_logic_vector(95 DOWNTO 0); -- Registrador interno do estágio IF/ID com 96 bits

BEGIN

	PROCESS (clk)
	BEGIN
		IF (rising_edge(clk)) THEN
			-- No pulso de subida do clock, os dados de entrada são armazenados no registrador IDIF
			IDIF(31 DOWNTO 0) <= instruction_in;       -- Armazena a instrução
			IDIF(63 DOWNTO 32) <= PC_in;        -- Armazena o PC de entrada
			IDIF(95 DOWNTO 64) <= PC_plus4_in;     -- Armazena o PC+4 de entrada
		END IF;
		IF (falling_edge(clk)) THEN
			-- No pulso de descida do clock, os dados armazenados no registrador IDIF são disponibilizados nas saídas
			PC_out <= IDIF(63 DOWNTO 32);       -- Fornece o PC de saída
			instruction_out <= IDIF(31 DOWNTO 0);      -- Fornece a instrução de saída
			PC_plus4_out <= IDIF(95 DOWNTO 64);    -- Fornece o PC+4 de saída
		END IF;
	END PROCESS;
	
END TypeArchitecture;

// VHDL entity IDEX, as the project stores it:
library ieee;
use ieee.std_logic_1164.all;

ENTITY IDEX IS
  PORT (
    clk              : IN  std_logic;                     -- Sinal de clock
    PC_in            : IN  std_logic_vector(31 DOWNTO 0); -- PC de entrada (Program Counter)
    read1_in         : IN  std_logic_vector(31 DOWNTO 0); -- Registrador de leitura 1 de entrada
    read2_in         : IN  std_logic_vector(31 DOWNTO 0); -- Registrador de leitura 2 de entrada
    immGen_in        : IN  std_logic_vector(31 DOWNTO 0); -- Saída do bloco "ImmGen" (gerador de imediatos) de entrada
    aluControl_in    : IN  std_logic_vector(3 downto 0);  -- Controle da ALU (Unidade Lógica e Aritmética) de entrada
    WB_address_in    : IN  std_logic_vector(4 downto 0);  -- Endereço do registrador de escrita de volta de entrada
    WB_in            : IN  std_logic_vector(2 downto 0);  -- Controle do estágio de escrita de volta (WB) de entrada
    Memory_in        : IN  std_logic_vector(5 downto 0);  -- Controle do estágio de memória (M) de entrada
    EX_control_in    : IN  std_logic_vector(6 downto 0);  -- Controle do estágio de execução (EX) de entrada
    PC_plus4_in      : IN  std_logic_vector(31 downto 0); -- PC + 4 de entrada
    PC_out           : OUT std_logic_vector(31 DOWNTO 0); -- PC de saída (Program Counter)

    read1_out        : OUT std_logic_vector(31 DOWNTO 0); -- Registrador de leitura 1 de saída
    read2_out        : OUT std_logic_vector(31 DOWNTO 0); -- Registrador de leitura 2 de saída
    immGen_out       : OUT std_logic_vector(31 DOWNTO 0); -- Saída do bloco "ImmGen" (gerador de imediatos) de saída
    aluControl_out   : OUT std_logic_vector(3 downto 0);  -- Controle da ALU (Unidade Lógica e Aritmética) de saída
    WB_address_out   : OUT std_logic_vector(4 downto 0);  -- Endereço do registrador de escrita de volta de saída
    WB_out           : OUT std_logic_vector(2 downto 0);  -- Controle do estágio de escrita de volta (WB) de saída
    Memory_out       : OUT std_logic_vector(5 downto 0);  -- Controle do estágio de memória (M) de saída
    EX_control_out   : OUT std_logic_vector(6 downto 0);  -- Controle do estágio de execução (EX) de saída
    PC_plus4_out     : OUT std_logic_vector(31 downto 0)  -- PC + 4 de saída
    );
END IDEX;

ARCHITECTURE TypeArchitecture OF IDEX IS

SIGNAL idex_sig : std_logic_vector(184 DOWNTO 0); -- Registrador interno do estágio IDEX com 185 bits

BEGIN

	PROCESS (clk)
	BEGIN
		IF (rising_edge(clk)) THEN
			-- No pulso de subida do clock, os dados de entrada são armazenados no registrador idex_sig
			idex_sig(31 DOWNTO 0)    <= PC_in;
			idex_sig(63 DOWNTO 32)   <= read1_in;
			idex_sig(95 DOWNTO 64)   <= read2_in;
			idex_sig(127 DOWNTO 96)  <= immGen_in;
			idex_sig(131 DOWNTO 128) <= aluControl_in;
			idex_sig(136 DOWNTO 132) <= WB_address_in;
			idex_sig(139 downto 137) <= WB_in;
			idex_sig(145 downto 140) <= Memory_in;
			idex_sig(152 downto 146) <= EX_control_in;
			idex_sig(184 downto 153) <= PC_plus4_in;
		END IF;
		IF (falling_edge(clk)) THEN
			-- No pulso de descida do clock, os dados armazenados no registrador idex_sig são disponibilizados nas saídas
			PC_out    <= idex_sig(31 DOWNTO 0);
			read1_out <= idex_sig(63 DOWNTO 32);
			read2_out <= idex_sig(95 DOWNTO 64);
			immGen_out <= idex_sig(127 DOWNTO 96);
			aluControl_out <= idex_sig(131 DOWNTO 128);
			WB_address_out <= idex_sig(136 DOWNTO 132);
			WB_out  <= idex_sig(139 downto 137);
			Memory_out <= idex_sig(145 downto 140);
			EX_control_out <= idex_sig(152 downto 146);
			PC_plus4_out <= idex_sig(184 downto 153);
		END IF;
	END PROCESS;
	
END TypeArchitecture;

// VHDL entity EXMEM, as the project stores it:
library ieee;
use ieee.std_logic_1164.all;

ENTITY EXMEM IS
  PORT (
    clk                : IN  std_logic;                     -- Sinal de clock
    ALUresult_in       : IN  std_logic_vector(31 DOWNTO 0); -- Resultado da ALU de entrada
    ALUzero_in         : IN  std_logic;                     -- Sinal indicando se a saída da ALU é zero de entrada
    ALUresult_in    : IN  std_logic_vector(31 DOWNTO 0); -- Saída da ALU de entrada
    read2_in           : IN  std_logic_vector(31 DOWNTO 0); -- Registrador de leitura 2 de entrada
    WB_address_in      : IN  std_logic_vector(4 downto 0);  -- Endereço do registrador de escrita de volta de entrada
    WB_in              : IN  std_logic_vector(2 downto 0);  -- Controle do estágio de escrita de volta (WB) de entrada
    Memory_in          : IN  std_logic_vector(5 downto 0);  -- Controle do estágio de memória (M) de entrada
    PC_plus4_in        : IN  std_logic_vector(31 downto 0); -- PC + 4 de entrada

    PC_out             : OUT std_logic_vector(31 DOWNTO 0); -- PC de saída (Program Counter)
    ALUzero_out        : OUT std_logic;                     -- Sinal indicando se a saída da ALU é zero de saída
    ALUresult_out   : OUT std_logic_vector(31 DOWNTO 0); -- Saída da ALU de saída
    read2_out          : OUT std_logic_vector(31 DOWNTO 0); -- Registrador de leitura 2 de saída
    WB_address_out     : OUT std_logic_vector(4 downto 0);  -- Endereço do registrador de escrita de volta de saída
    WB_out             : OUT std_logic_vector(2 downto 0);  -- Controle do estágio de escrita de volta (WB) de saída
    Memory_out         : OUT std_logic_vector(5 downto 0);  -- Controle do estágio de memória (M) de saída
    PC_plus4_out       : OUT std_logic_vector(31 downto 0)  -- PC + 4 de saída
    );
END EXMEM;

ARCHITECTURE TypeArchitecture OF EXMEM IS

SIGNAL exmem_sig : std_logic_vector(142 DOWNTO 0); -- Registrador interno do estágio EXMEM com 143 bits

BEGIN

	PROCESS (clk)
	BEGIN
		IF (rising_edge(clk)) THEN
			-- No pulso de subida do clock, os dados de entrada são armazenados no registrador exmem_sig
			exmem_sig(31 DOWNTO 0)   <= sum_address_in;
			exmem_sig(32)  <= ALUzero_in;
			exmem_sig(64 DOWNTO 33)  <= ALUresult_in;
			exmem_sig(96 DOWNTO 65) <= read2_in;
			exmem_sig(101 DOWNTO 97) <= WB_address_in;
			exmem_sig(104 DOWNTO 102) <= WB_in;
			exmem_sig(110 DOWNTO 105) <= Memory_in;
			exmem_sig(142 downto 111) <= PC_plus4_in;
		END IF;
		IF (falling_edge(clk)) THEN
			-- No pulso de descida do clock, os dados armazenados no registrador exmem_sig são disponibilizados nas saídas
			PC_out    <= exmem_sig(31 DOWNTO 0);
			
			if (exmem_sig(32) = 'U') then
				ALUzero_out <= '0';
			else
				ALUzero_out <= exmem_sig(32);
			end if; 

			if (exmem_sig(64 DOWNTO 33) = "UUUUUUUUUUUUUUUUUUUUUUUUUUUUUUUU") then
				ALUresult_out <= "00000000000000000000000000000000";
			else
				ALUresult_out <= exmem_sig(64 DOWNTO 33);
			end if;
			
			read2_out <= exmem_sig(96 DOWNTO 65);
			WB_address_out <= exmem_sig(101 DOWNTO 97);
			
			if (exmem_sig(110 DOWNTO 105) = "UUUUUU") then
				Memory_out <= "000000";
			else
				Memory_out <= exmem_sig(110 DOWNTO 105);
			end if;
			
			WB_out  <= exmem_sig(104 DOWNTO 102);

			PC_plus4_out <= exmem_sig(142 downto 111);
			
			
		END IF;
	END PROCESS;
	
END TypeArchitecture;

// VHDL entity MEMWB, as the project stores it:
library ieee;
use ieee.std_logic_1164.all;

ENTITY MEMWB IS
  PORT (
    clk                 : IN  std_logic;                     -- Sinal de clock
    mem_read_in         : IN  std_logic_vector(31 DOWNTO 0); -- Dado lido da memória de entrada
    ALUresult_in     : IN  std_logic_vector(31 DOWNTO 0); -- Saída da ALU de entrada
    WB_address_in       : IN  std_logic_vector(4 downto 0);  -- Endereço do registrador de escrita de volta de entrada
    WB_in               : IN  std_logic_vector(2 downto 0);  -- Controle do estágio de escrita de volta (WB) de entrada
    PC_plus4_in         : IN  std_logic_vector(31 downto 0); -- PC + 4 de entrada
    PC_plusAddress_in   : IN  std_logic_vector(31 downto 0); -- PC + Instrução de 32 bits de entrada

    mem_read_out        : OUT std_logic_vector(31 DOWNTO 0); -- Dado lido da memória de saída
    ALUresult_out    : OUT std_logic_vector(31 DOWNTO 0); -- Saída da ALU de saída
    WB_address_out      : OUT std_logic_vector(4 downto 0);  -- Endereço do registrador de escrita de volta de saída
    WB_out              : OUT std_logic_vector(2 downto 0);  -- Controle do estágio de escrita de volta (WB) de saída
    PC_plus4_out        : OUT std_logic_vector(31 downto 0); -- PC + 4 de saída
    PC_plusAddress_out  : OUT std_logic_vector(31 downto 0)  -- PC + Instrução de 32 bits de saída
    );
END MEMWB;

ARCHITECTURE TypeArchitecture OF MEMWB IS

SIGNAL memwb_sig : std_logic_vector(135 DOWNTO 0); -- Registrador interno do estágio MEMWB com 136 bits

BEGIN

	PROCESS (clk)
	BEGIN
		IF (rising_edge(clk)) THEN
			-- No pulso de subida do clock, os dados de entrada são armazenados no registrador memwb_sig
			memwb_sig(31 DOWNTO 0)   <= mem_read_in;
			memwb_sig(63 DOWNTO 32)  <= ALUresult_in;
			memwb_sig(68 DOWNTO 64)  <= WB_address_in;
			memwb_sig(71 DOWNTO 69)  <= WB_in;
			memwb_sig(103 downto 72) <= PC_plus4_in;
			memwb_sig(135 downto 104) <= PC_plusAddress_in;
			
		END IF;
		IF (falling_edge(clk)) THEN
			-- No pulso de descida do clock, os dados armazenados no registrador memwb_sig são disponibilizados nas saídas
			mem_read_out    <=  memwb_sig(31 DOWNTO 0);
			ALUresult_out  <=  memwb_sig(63 DOWNTO 32);
			WB_address_out <= memwb_sig(68 DOWNTO 64);
			WB_out  <= memwb_sig(71 DOWNTO 69);
			PC_plus4_out <= memwb_sig(103 downto 72);
			PC_plusAddress_out
 <= memwb_sig(135 downto 104);
		END IF;
	END PROCESS;
	
END TypeArchitecture;
